// Digital circuit RV32I-ALU-Input.dig as structural Verilog
module RV32I_ALU_Input (
  input  [31:0] INSTR,
  input  [23:0] PC,
  input  [31:0] RS1,
  input  [31:0] RS2,
  output [31:0] A,
  output [31:0] B,
  output [31:0] COMP_A,
  output [31:0] COMP_B
);

  wire I, I_B, I_I, I_J, I_R, I_S, I_U, not_1_out, PC_t, RS1_t, RS2_t, ZERO;
  wire [0:0] pulldown_4_out;
  wire [10:0] pulldown_3_out;
  wire [11:0] pulldown_2_out;
  wire [18:0] pulldown_6_out;
  wire [19:0] pulldown_5_out;
  wire [31:0] driver_8_out;
  wire [31:24] pulldown_1_out;

  PullDown #(.Bits(8)) pulldown_1 (.out(pulldown_1_out));
  RV32I_ALU_Input_Instruction_Decoder rv32i_alu_input_instruction_decoder_1 (
    .IN(INSTR), .FORMAT({I_J, I_U, I_B, I_S, I_I, I_R}), .ALU_A_SOURCE({ZERO, PC_t, RS1_t}),
    .ALU_B_SOURCE({RS2_t, I}));
  PullDown #(.Bits(12)) pulldown_2 (.out(pulldown_2_out));
  PullDown #(.Bits(11)) pulldown_3 (.out(pulldown_3_out));
  PullDown pulldown_4 (.out(pulldown_4_out[0]));
  PullDown #(.Bits(20)) pulldown_5 (.out(pulldown_5_out));
  PullDown #(.Bits(19)) pulldown_6 (.out(pulldown_6_out));
  not not_1 (not_1_out, I_I);
  assign COMP_B = I_I ? {pulldown_5_out, INSTR[31:20]} : 32'bz;  // Driver driver_1
  assign COMP_B = not_1_out ? RS2 : 32'bz;  // Driver driver_2
  assign A = PC_t ? {pulldown_1_out, PC} : 32'bz;  // Driver driver_3
  assign A = RS1_t ? RS1 : 32'bz;  // Driver driver_4
  assign A = ZERO ? {32{1'b0}} : 32'bz;  // Driver driver_5
  assign B = RS2_t ? RS2 : 32'bz;  // Driver driver_6
  assign B = I ? driver_8_out : 32'bz;  // Driver driver_7
  assign driver_8_out = I_I ? {pulldown_5_out, INSTR[31:20]} : 32'bz;  // Driver driver_8
  assign driver_8_out = I_S ? {pulldown_5_out, INSTR[31:25], INSTR[11:7]} : 32'bz;  // Driver driver_9
  assign driver_8_out = I_B ? {pulldown_6_out, INSTR[31], INSTR[7], INSTR[30:25], INSTR[11:8], pulldown_4_out[0]} : 32'bz;  // Driver driver_10
  assign driver_8_out = I_U ? {INSTR[31:12], pulldown_2_out} : 32'bz;  // Driver driver_11
  assign driver_8_out = I_J ? {pulldown_3_out, INSTR[31], INSTR[19:12], INSTR[20], INSTR[30:21], pulldown_4_out[0]} : 32'bz;  // Driver driver_12

  assign COMP_A = RS1;
endmodule
