// Digital circuit RV32I-ALU.dig as structural Verilog
module RV32I_ALU (
  input  [31:0] A,
  input  [31:0] B,
  input  [7:0] O,
  output [31:0] Y
);

  wire pulldown_1_out;
  wire [5:5] pulldown_2_out, pulldown_3_out, pulldown_4_out;
  wire [31:0] ADD_s, and_1_out, or_1_out, SLL_out, SRA_out, SRL_out, SUB_s, xor_1_out;

  PullDown pulldown_1 (.out(pulldown_1_out));
  Add #(.Bits(32)) ADD (.a(A), .b(B), .c_i(pulldown_1_out), .s(ADD_s));  // open: c_o
  Add #(.Bits(32)) SUB (.a(A), .b(B), .c_i(pulldown_1_out), .s(SUB_s));  // open: c_o
  assign and_1_out = A & B;  // And and_1, 32 bits wide
  assign or_1_out = A | B;  // Or or_1, 32 bits wide
  assign xor_1_out = A ^ B;  // XOr xor_1, 32 bits wide
  PullDown pulldown_2 (.out(pulldown_2_out[5]));
  PullDown pulldown_3 (.out(pulldown_3_out[5]));
  PullDown pulldown_4 (.out(pulldown_4_out[5]));
  BarrelShifter #(.Bits(32)) SLL (.in(A), .shift({pulldown_2_out[5], B[4:0]}), .out(SLL_out));
  BarrelShifter #(.Bits(32), .direction("right")) SRL (.in(A), .shift({pulldown_3_out[5], B[4:0]}), .out(SRL_out));
  BarrelShifter #(.Bits(32), .barrelShifterMode("arithmetic"), .direction("right")) SRA (
    .in(A), .shift({pulldown_4_out[5], B[4:0]}), .out(SRA_out));
  assign Y = O[0] ? ADD_s : 32'bz;  // Driver driver_1
  assign Y = O[4] ? SUB_s : 32'bz;  // Driver driver_2
  assign Y = O[2] ? and_1_out : 32'bz;  // Driver driver_3
  assign Y = O[1] ? or_1_out : 32'bz;  // Driver driver_4
  assign Y = O[5] ? xor_1_out : 32'bz;  // Driver driver_5
  assign Y = O[6] ? SLL_out : 32'bz;  // Driver driver_6
  assign Y = O[3] ? SRL_out : 32'bz;  // Driver driver_7
  assign Y = O[7] ? SRA_out : 32'bz;  // Driver driver_8

  // Other names for the same wires on the sheet: ADD = O[0]; OR = O[1]; AND = O[2]; SRL = O[3]; SUB = O[4];
  //   XOR = O[5]; SLL = O[6]; SRA = O[7]
endmodule
