// Digital circuit RV32I-Control.dig as structural Verilog
module RV32I_Control (
  input  START,
  input  PAUSE,
  input  RESET,
  input  HOLD,
  input  SET_ERROR,
  input  BC,
  input  BCO,
  input  CLC,
  output NORMAL,
  output RUN,
  output GO,
  output ERROR,
  output BCE,
  output BC_SET_R_W_A,
  output ROM_SET_MEM_R_W
);

  wire and_1_out, and_2_out, and_3_out, jk_ff_1_nq, or_1_out, or_2_out, Pause_Run_nq;

  JK_FF jk_ff_1 (.J(START), .C(CLC), .K(~START), .nQ(jk_ff_1_nq));  // open: Q
  and and_1 (and_1_out, START, jk_ff_1_nq);
  or or_1 (or_1_out, RESET, NORMAL);
  or or_2 (or_2_out, and_1_out, Pause_Run_nq);
  and and_2 (and_2_out, or_1_out, ~BC, ~BCO);  // And
  and and_3 (and_3_out, or_2_out, ~PAUSE);  // And
  D_FF Boot_Normal (.D(and_2_out), .C(CLC), .Q(NORMAL), .nQ(BC_SET_R_W_A));
  D_FF #(.Default(1)) Pause_Run (.D(and_3_out), .C(CLC), .Q(RUN), .nQ(Pause_Run_nq));
  not not_1 (GO, HOLD);
  and and_4 (BCE, BC_SET_R_W_A, RUN);

  assign ERROR = SET_ERROR;
  assign ROM_SET_MEM_R_W = BC_SET_R_W_A;

  // Notes on the sheet:
  //   STATUS
endmodule
