// Digital circuit RV32I-Decode-Control.dig as structural Verilog
module RV32I_Decode_Control (
  input  [31:0] INSTR,
  input  Normal,
  input  Run,
  input  Go,
  output DECODE_HOLD,
  output DECODE_EN,
  output RESERVE,
  output ERROR
);

  wire rv32i_decode_instruction_decoder_1_rd, rv32i_decode_instruction_decoder_1_rs1, undriven, undriven_2,
       undriven_3;

  RV32I_Decode_Instruction_Decoder rv32i_decode_instruction_decoder_1 (
    .IN(INSTR), .RD(rv32i_decode_instruction_decoder_1_rd), .RS1(rv32i_decode_instruction_decoder_1_rs1));  // open: RS2, E
  and and_1 (DECODE_HOLD, ~undriven, undriven_2, undriven_3);  // And
  and and_2 (DECODE_EN, Normal, Run);
  and and_3 (RESERVE, rv32i_decode_instruction_decoder_1_rd, Normal, Run, Go);
  and and_4 (ERROR, rv32i_decode_instruction_decoder_1_rs1, Run, Normal, Go);
  // Pins of 4 and 32 bits meet at INSTR
endmodule
