// Digital circuit RV32I-Execute-Control.dig as structural Verilog
module RV32I_Execute_Control (
  input  [31:0] INSTR,
  input  Normal,
  input  Run,
  input  COMP,
  output EXECUTE_HOLD,
  output EXECUTE_EN,
  output [7:0] ALU_INSTR,
  output [7:0] COMP_SEL,
  output [4:0] RS1_A,
  output [4:0] RS2_A,
  output JUMP
);

  wire and_2_out;
  wire [1:0] rv32i_execute_instruction_decoder_1_jump;

  RV32I_Execute_Instruction_Decoder rv32i_execute_instruction_decoder_1 (
    .IN(INSTR), .ALU_INSTR(ALU_INSTR), .COMP_SEL(COMP_SEL), .JUMP(rv32i_execute_instruction_decoder_1_jump));
  and and_1 (EXECUTE_HOLD, ~INSTR[4], INSTR[5], INSTR[6]);  // And
  and and_2 (and_2_out, rv32i_execute_instruction_decoder_1_jump[1], COMP);
  and and_3 (EXECUTE_EN, Normal, Run);
  or or_1 (JUMP, rv32i_execute_instruction_decoder_1_jump[0], and_2_out);

  assign RS1_A = INSTR[19:15];
  assign RS2_A = INSTR[24:20];
endmodule
