// Digital circuit RV32I-Fetch-Control.dig as structural Verilog
module RV32I_Fetch_Control (
  input  Normal,
  input  Run,
  input  Go,
  input  ALU_SET_PC,
  output PC_EN,
  output Memory_Store,
  output PC_Incrementer_Set_PC,
  output PC_STALL
);

  and and_1 (PC_EN, Normal, Run);
  not not_1 (Memory_Store, Normal);
  and and_2 (PC_Incrementer_Set_PC, Go, ~ALU_SET_PC);  // And
  and and_3 (PC_STALL, ~Go, ~ALU_SET_PC);  // And
endmodule
