// Digital circuit RV32I-Instruction-Display.dig as structural Verilog
module RV32I_Instruction_Display (
  input  [31:0] INSTR,
  output [15:0] _0,
  output D0,
  output [15:0] _1,
  output D1,
  output [15:0] _2,
  output D2,
  output [15:0] _3,
  output D3,
  output [15:0] _4,
  output D4,
  output [15:0] _5,
  output D5,
  output [15:0] _6,
  output D6,
  output [15:0] _7,
  output D7
);

  wire and_1_out, and_2_out, and_3_out, and_4_out, and_5_out, and_6_out, and_7_out, and_8_out, and_9_out,
       and_10_out, and_11_out, and_12_out, and_13_out, and_14_out, and_15_out, and_16_out, and_17_out,
       and_18_out, and_19_out, and_20_out, and_21_out, and_22_out, and_23_out, and_24_out, and_25_out,
       and_26_out, and_27_out, and_28_out, and_29_out, and_30_out, and_31_out, and_32_out, and_33_out,
       and_34_out, and_35_out, and_36_out, and_37_out, and_38_out, nor_1_out;

  and and_1 (and_1_out, INSTR[0], INSTR[1], ~INSTR[2], ~INSTR[3], INSTR[4], INSTR[5], ~INSTR[6], ~INSTR[12], ~INSTR[13], ~INSTR[14], ~INSTR[25], ~INSTR[26], ~INSTR[27], ~INSTR[28], ~INSTR[29], ~INSTR[30], ~INSTR[31]);  // And
  and and_2 (and_2_out, INSTR[0], INSTR[1], ~INSTR[2], ~INSTR[3], INSTR[4], INSTR[5], ~INSTR[6], ~INSTR[12], ~INSTR[13], ~INSTR[14], ~INSTR[25], ~INSTR[26], ~INSTR[27], ~INSTR[28], ~INSTR[29], INSTR[30], ~INSTR[31]);  // And
  and and_3 (and_3_out, INSTR[0], INSTR[1], ~INSTR[2], ~INSTR[3], INSTR[4], INSTR[5], ~INSTR[6], INSTR[12], INSTR[13], INSTR[14], ~INSTR[25], ~INSTR[26], ~INSTR[27], ~INSTR[28], ~INSTR[29], ~INSTR[30], ~INSTR[31]);  // And
  and and_4 (and_4_out, INSTR[0], INSTR[1], ~INSTR[2], ~INSTR[3], INSTR[4], INSTR[5], ~INSTR[6], ~INSTR[12], INSTR[13], INSTR[14], ~INSTR[25], ~INSTR[26], ~INSTR[27], ~INSTR[28], ~INSTR[29], ~INSTR[30], ~INSTR[31]);  // And
  and and_5 (and_5_out, INSTR[0], INSTR[1], ~INSTR[2], ~INSTR[3], INSTR[4], INSTR[5], ~INSTR[6], ~INSTR[12], ~INSTR[13], INSTR[14], ~INSTR[25], ~INSTR[26], ~INSTR[27], ~INSTR[28], ~INSTR[29], ~INSTR[30], ~INSTR[31]);  // And
  and and_6 (and_6_out, INSTR[0], INSTR[1], ~INSTR[2], ~INSTR[3], INSTR[4], ~INSTR[5], ~INSTR[6], ~INSTR[12], ~INSTR[13], ~INSTR[14], ~INSTR[25], ~INSTR[26], ~INSTR[27], ~INSTR[28], ~INSTR[29], ~INSTR[30], ~INSTR[31]);  // And
  and and_7 (and_7_out, INSTR[0], INSTR[1], ~INSTR[2], ~INSTR[3], INSTR[4], ~INSTR[5], ~INSTR[6], INSTR[12], INSTR[13], INSTR[14], ~INSTR[25], ~INSTR[26], ~INSTR[27], ~INSTR[28], ~INSTR[29], ~INSTR[30], ~INSTR[31]);  // And
  and and_8 (and_8_out, INSTR[0], INSTR[1], ~INSTR[2], ~INSTR[3], INSTR[4], ~INSTR[5], ~INSTR[6], ~INSTR[12], INSTR[13], INSTR[14], ~INSTR[25], ~INSTR[26], ~INSTR[27], ~INSTR[28], ~INSTR[29], ~INSTR[30], ~INSTR[31]);  // And
  and and_9 (and_9_out, INSTR[0], INSTR[1], ~INSTR[2], ~INSTR[3], INSTR[4], ~INSTR[5], ~INSTR[6], ~INSTR[12], ~INSTR[13], INSTR[14], ~INSTR[25], ~INSTR[26], ~INSTR[27], ~INSTR[28], ~INSTR[29], ~INSTR[30], ~INSTR[31]);  // And
  and and_10 (and_10_out, INSTR[0], INSTR[1], ~INSTR[2], ~INSTR[3], INSTR[4], INSTR[5], ~INSTR[6], INSTR[12], ~INSTR[13], ~INSTR[14], ~INSTR[25], ~INSTR[26], ~INSTR[27], ~INSTR[28], ~INSTR[29], ~INSTR[30], ~INSTR[31]);  // And
  and and_11 (and_11_out, INSTR[0], INSTR[1], ~INSTR[2], ~INSTR[3], INSTR[4], INSTR[5], ~INSTR[6], INSTR[12], ~INSTR[13], INSTR[14], ~INSTR[25], ~INSTR[26], ~INSTR[27], ~INSTR[28], ~INSTR[29], ~INSTR[30], ~INSTR[31]);  // And
  and and_12 (and_12_out, INSTR[0], INSTR[1], ~INSTR[2], ~INSTR[3], INSTR[4], INSTR[5], ~INSTR[6], INSTR[12], ~INSTR[13], INSTR[14], ~INSTR[25], ~INSTR[26], ~INSTR[27], ~INSTR[28], ~INSTR[29], INSTR[30], ~INSTR[31]);  // And
  and and_13 (and_13_out, INSTR[0], INSTR[1], ~INSTR[2], ~INSTR[3], INSTR[4], ~INSTR[5], ~INSTR[6], INSTR[12], ~INSTR[13], ~INSTR[14], ~INSTR[25], ~INSTR[26], ~INSTR[27], ~INSTR[28], ~INSTR[29], ~INSTR[30], ~INSTR[31]);  // And
  and and_14 (and_14_out, INSTR[0], INSTR[1], ~INSTR[2], ~INSTR[3], INSTR[4], ~INSTR[5], ~INSTR[6], INSTR[12], ~INSTR[13], INSTR[14], ~INSTR[25], ~INSTR[26], ~INSTR[27], ~INSTR[28], ~INSTR[29], ~INSTR[30], ~INSTR[31]);  // And
  and and_15 (and_15_out, INSTR[0], INSTR[1], ~INSTR[2], ~INSTR[3], INSTR[4], ~INSTR[5], ~INSTR[6], INSTR[12], ~INSTR[13], INSTR[14], ~INSTR[25], ~INSTR[26], ~INSTR[27], ~INSTR[28], ~INSTR[29], INSTR[30], ~INSTR[31]);  // And
  and and_16 (and_16_out, INSTR[0], INSTR[1], ~INSTR[2], ~INSTR[3], INSTR[4], INSTR[5], ~INSTR[6], ~INSTR[12], INSTR[13], ~INSTR[14], ~INSTR[25], ~INSTR[26], ~INSTR[27], ~INSTR[28], ~INSTR[29], ~INSTR[30], ~INSTR[31]);  // And
  and and_17 (and_17_out, INSTR[0], INSTR[1], ~INSTR[2], ~INSTR[3], INSTR[4], INSTR[5], ~INSTR[6], INSTR[12], INSTR[13], ~INSTR[14], ~INSTR[25], ~INSTR[26], ~INSTR[27], ~INSTR[28], ~INSTR[29], ~INSTR[30], ~INSTR[31]);  // And
  and and_18 (and_18_out, INSTR[0], INSTR[1], ~INSTR[2], ~INSTR[3], INSTR[4], ~INSTR[5], ~INSTR[6], ~INSTR[12], INSTR[13], ~INSTR[14], ~INSTR[25], ~INSTR[26], ~INSTR[27], ~INSTR[28], ~INSTR[29], ~INSTR[30], ~INSTR[31]);  // And
  and and_19 (and_19_out, INSTR[0], INSTR[1], ~INSTR[2], ~INSTR[3], INSTR[4], ~INSTR[5], ~INSTR[6], INSTR[12], INSTR[13], ~INSTR[14], ~INSTR[25], ~INSTR[26], ~INSTR[27], ~INSTR[28], ~INSTR[29], ~INSTR[30], ~INSTR[31]);  // And
  and and_20 (and_20_out, INSTR[0], INSTR[1], INSTR[2], ~INSTR[3], INSTR[4], INSTR[5], ~INSTR[6]);  // And
  and and_21 (and_21_out, INSTR[0], INSTR[1], INSTR[2], ~INSTR[3], INSTR[4], ~INSTR[5], ~INSTR[6]);  // And
  and and_22 (and_22_out, INSTR[0], INSTR[1], INSTR[2], INSTR[3], ~INSTR[4], INSTR[5], INSTR[6]);  // And
  and and_23 (and_23_out, INSTR[0], INSTR[1], INSTR[2], ~INSTR[3], ~INSTR[4], INSTR[5], INSTR[6], ~INSTR[12], ~INSTR[13], ~INSTR[14]);  // And
  and and_24 (and_24_out, INSTR[0], INSTR[1], ~INSTR[2], ~INSTR[3], ~INSTR[4], INSTR[5], INSTR[6], ~INSTR[12], ~INSTR[13], ~INSTR[14]);  // And
  and and_25 (and_25_out, INSTR[0], INSTR[1], ~INSTR[2], ~INSTR[3], ~INSTR[4], INSTR[5], INSTR[6], INSTR[12], ~INSTR[13], ~INSTR[14]);  // And
  and and_26 (and_26_out, INSTR[0], INSTR[1], ~INSTR[2], ~INSTR[3], ~INSTR[4], INSTR[5], INSTR[6], ~INSTR[12], ~INSTR[13], INSTR[14]);  // And
  and and_27 (and_27_out, INSTR[0], INSTR[1], ~INSTR[2], ~INSTR[3], ~INSTR[4], INSTR[5], INSTR[6], INSTR[12], ~INSTR[13], INSTR[14]);  // And
  and and_28 (and_28_out, INSTR[0], INSTR[1], ~INSTR[2], ~INSTR[3], ~INSTR[4], INSTR[5], INSTR[6], ~INSTR[12], INSTR[13], INSTR[14]);  // And
  and and_29 (and_29_out, INSTR[0], INSTR[1], ~INSTR[2], ~INSTR[3], ~INSTR[4], INSTR[5], INSTR[6], INSTR[12], INSTR[13], INSTR[14]);  // And
  and and_30 (and_30_out, INSTR[0], INSTR[1], ~INSTR[2], ~INSTR[3], ~INSTR[4], ~INSTR[5], ~INSTR[6], ~INSTR[12], ~INSTR[13], ~INSTR[14]);  // And
  and and_31 (and_31_out, INSTR[0], INSTR[1], ~INSTR[2], ~INSTR[3], ~INSTR[4], ~INSTR[5], ~INSTR[6], INSTR[12], ~INSTR[13], ~INSTR[14]);  // And
  and and_32 (and_32_out, INSTR[0], INSTR[1], ~INSTR[2], ~INSTR[3], ~INSTR[4], ~INSTR[5], ~INSTR[6], ~INSTR[12], INSTR[13], ~INSTR[14]);  // And
  and and_33 (and_33_out, INSTR[0], INSTR[1], ~INSTR[2], ~INSTR[3], ~INSTR[4], ~INSTR[5], ~INSTR[6], ~INSTR[12], ~INSTR[13], INSTR[14]);  // And
  and and_34 (and_34_out, INSTR[0], INSTR[1], ~INSTR[2], ~INSTR[3], ~INSTR[4], ~INSTR[5], ~INSTR[6], INSTR[12], ~INSTR[13], INSTR[14]);  // And
  and and_35 (and_35_out, INSTR[0], INSTR[1], ~INSTR[2], ~INSTR[3], ~INSTR[4], INSTR[5], ~INSTR[6], ~INSTR[12], ~INSTR[13], ~INSTR[14]);  // And
  and and_36 (and_36_out, INSTR[0], INSTR[1], ~INSTR[2], ~INSTR[3], ~INSTR[4], INSTR[5], ~INSTR[6], INSTR[12], ~INSTR[13], ~INSTR[14]);  // And
  and and_37 (and_37_out, INSTR[0], INSTR[1], ~INSTR[2], ~INSTR[3], ~INSTR[4], INSTR[5], ~INSTR[6], ~INSTR[12], INSTR[13], ~INSTR[14]);  // And
  and and_38 (and_38_out, ~INSTR[0], ~INSTR[1], ~INSTR[2], ~INSTR[3], ~INSTR[4], ~INSTR[5], ~INSTR[6], ~INSTR[7], ~INSTR[8], ~INSTR[9], ~INSTR[10], ~INSTR[11], ~INSTR[12], ~INSTR[13], ~INSTR[14], ~INSTR[15], ~INSTR[16], ~INSTR[17], ~INSTR[18], ~INSTR[19], ~INSTR[20], ~INSTR[21], ~INSTR[22], ~INSTR[23], ~INSTR[24], ~INSTR[25], ~INSTR[26], ~INSTR[27], ~INSTR[28], ~INSTR[29], ~INSTR[30], ~INSTR[31]);  // And
  nor nor_1 (nor_1_out, and_1_out, and_2_out, and_3_out, and_4_out, and_5_out, and_6_out, and_7_out, and_8_out, and_9_out, and_10_out, and_11_out, and_12_out, and_13_out, and_14_out, and_15_out, and_16_out, and_17_out, and_18_out, and_19_out, and_20_out, and_21_out, and_22_out, and_23_out, and_24_out, and_25_out, and_26_out, and_27_out, and_28_out, and_29_out, and_30_out, and_31_out, and_32_out, and_33_out, and_34_out, and_35_out, and_36_out, and_37_out, and_38_out);
  assign _5 = and_1_out ? 16'h3cf : 16'bz;  // Driver driver_1
  assign _6 = and_1_out ? 16'h483f : 16'bz;  // Driver driver_2
  assign _7 = and_1_out ? 16'h483f : 16'bz;  // Driver driver_3
  assign _5 = and_2_out ? 16'h63b : 16'bz;  // Driver driver_4
  assign _6 = and_2_out ? 16'hfc : 16'bz;  // Driver driver_5
  assign _7 = and_2_out ? 16'h4a3f : 16'bz;  // Driver driver_6
  assign _5 = and_3_out ? 16'h3cf : 16'bz;  // Driver driver_7
  assign _6 = and_3_out ? 16'h24cc : 16'bz;  // Driver driver_8
  assign _7 = and_3_out ? 16'h483f : 16'bz;  // Driver driver_9
  assign _6 = and_4_out ? 16'hff : 16'bz;  // Driver driver_10
  assign _7 = and_4_out ? 16'h23c7 : 16'bz;  // Driver driver_11
  assign _5 = and_5_out ? 16'hb400 : 16'bz;  // Driver driver_12
  assign _6 = and_5_out ? 16'hff : 16'bz;  // Driver driver_13
  assign _7 = and_5_out ? 16'h23c7 : 16'bz;  // Driver driver_14
  assign _4 = and_6_out ? 16'h3cf : 16'bz;  // Driver driver_15
  assign _5 = and_6_out ? 16'h483f : 16'bz;  // Driver driver_16
  assign _6 = and_6_out ? 16'h483f : 16'bz;  // Driver driver_17
  assign _7 = and_6_out ? 16'h4833 : 16'bz;  // Driver driver_18
  assign _4 = and_7_out ? 16'h3cf : 16'bz;  // Driver driver_19
  assign _5 = and_7_out ? 16'h24cc : 16'bz;  // Driver driver_20
  assign _6 = and_7_out ? 16'h483f : 16'bz;  // Driver driver_21
  assign _7 = and_7_out ? 16'h4833 : 16'bz;  // Driver driver_22
  assign _5 = and_8_out ? 16'hff : 16'bz;  // Driver driver_23
  assign _6 = and_8_out ? 16'h23c7 : 16'bz;  // Driver driver_24
  assign _7 = and_8_out ? 16'h4833 : 16'bz;  // Driver driver_25
  assign _4 = and_9_out ? 16'hb400 : 16'bz;  // Driver driver_26
  assign _5 = and_9_out ? 16'hff : 16'bz;  // Driver driver_27
  assign _6 = and_9_out ? 16'h23c7 : 16'bz;  // Driver driver_28
  assign _7 = and_9_out ? 16'h4833 : 16'bz;  // Driver driver_29
  assign _5 = and_10_out ? 16'h63b : 16'bz;  // Driver driver_30
  assign _6 = and_10_out ? 16'hf0 : 16'bz;  // Driver driver_31
  assign _7 = and_10_out ? 16'hf0 : 16'bz;  // Driver driver_32
  assign _5 = and_11_out ? 16'h63b : 16'bz;  // Driver driver_33
  assign _6 = and_11_out ? 16'h23c7 : 16'bz;  // Driver driver_34
  assign _7 = and_11_out ? 16'hf0 : 16'bz;  // Driver driver_35
  assign _5 = and_12_out ? 16'h63b : 16'bz;  // Driver driver_36
  assign _6 = and_12_out ? 16'h23c7 : 16'bz;  // Driver driver_37
  assign _7 = and_12_out ? 16'h3cf : 16'bz;  // Driver driver_38
  assign _4 = and_13_out ? 16'h63b : 16'bz;  // Driver driver_39
  assign _5 = and_13_out ? 16'hf0 : 16'bz;  // Driver driver_40
  assign _6 = and_13_out ? 16'hf0 : 16'bz;  // Driver driver_41
  assign _7 = and_13_out ? 16'h4833 : 16'bz;  // Driver driver_42
  assign _4 = and_14_out ? 16'h63b : 16'bz;  // Driver driver_43
  assign _5 = and_14_out ? 16'h23c7 : 16'bz;  // Driver driver_44
  assign _6 = and_14_out ? 16'hf0 : 16'bz;  // Driver driver_45
  assign _7 = and_14_out ? 16'h4833 : 16'bz;  // Driver driver_46
  assign _4 = and_15_out ? 16'h63b : 16'bz;  // Driver driver_47
  assign _5 = and_15_out ? 16'h23c7 : 16'bz;  // Driver driver_48
  assign _6 = and_15_out ? 16'h3cf : 16'bz;  // Driver driver_49
  assign _7 = and_15_out ? 16'h4833 : 16'bz;  // Driver driver_50
  assign _5 = and_16_out ? 16'h63b : 16'bz;  // Driver driver_51
  assign _6 = and_16_out ? 16'hf0 : 16'bz;  // Driver driver_52
  assign _7 = and_16_out ? 16'h4803 : 16'bz;  // Driver driver_53
  assign _4 = and_17_out ? 16'h63b : 16'bz;  // Driver driver_54
  assign _5 = and_17_out ? 16'hf0 : 16'bz;  // Driver driver_55
  assign _6 = and_17_out ? 16'h4803 : 16'bz;  // Driver driver_56
  assign _7 = and_17_out ? 16'hfc : 16'bz;  // Driver driver_57
  assign _4 = and_18_out ? 16'h63b : 16'bz;  // Driver driver_58
  assign _5 = and_18_out ? 16'hf0 : 16'bz;  // Driver driver_59
  assign _6 = and_18_out ? 16'h4803 : 16'bz;  // Driver driver_60
  assign _7 = and_18_out ? 16'h4833 : 16'bz;  // Driver driver_61
  assign _3 = and_19_out ? 16'h63b : 16'bz;  // Driver driver_62
  assign _4 = and_19_out ? 16'hf0 : 16'bz;  // Driver driver_63
  assign _5 = and_19_out ? 16'h4803 : 16'bz;  // Driver driver_64
  assign _6 = and_19_out ? 16'h4833 : 16'bz;  // Driver driver_65
  assign _7 = and_19_out ? 16'hfc : 16'bz;  // Driver driver_66
  assign _5 = and_20_out ? 16'hf0 : 16'bz;  // Driver driver_67
  assign _6 = and_20_out ? 16'hfc : 16'bz;  // Driver driver_68
  assign _7 = and_20_out ? 16'h4833 : 16'bz;  // Driver driver_69
  assign _3 = and_21_out ? 16'h3cf : 16'bz;  // Driver driver_70
  assign _4 = and_21_out ? 16'hfc : 16'bz;  // Driver driver_71
  assign _5 = and_21_out ? 16'h4833 : 16'bz;  // Driver driver_72
  assign _6 = and_21_out ? 16'h3c7 : 16'bz;  // Driver driver_73
  assign _7 = and_21_out ? 16'hf3 : 16'bz;  // Driver driver_74
  assign _5 = and_22_out ? 16'h7c : 16'bz;  // Driver driver_75
  assign _6 = and_22_out ? 16'h3cf : 16'bz;  // Driver driver_76
  assign _7 = and_22_out ? 16'hf0 : 16'bz;  // Driver driver_77
  assign _4 = and_23_out ? 16'h7c : 16'bz;  // Driver driver_78
  assign _5 = and_23_out ? 16'h3cf : 16'bz;  // Driver driver_79
  assign _6 = and_23_out ? 16'hf0 : 16'bz;  // Driver driver_80
  assign _7 = and_23_out ? 16'h23c7 : 16'bz;  // Driver driver_81
  assign _5 = and_24_out ? 16'h4a3f : 16'bz;  // Driver driver_82
  assign _6 = and_24_out ? 16'h3f3 : 16'bz;  // Driver driver_83
  assign _7 = and_24_out ? 16'h20ff : 16'bz;  // Driver driver_84
  assign _5 = and_25_out ? 16'h4a3f : 16'bz;  // Driver driver_85
  assign _6 = and_25_out ? 16'h24cc : 16'bz;  // Driver driver_86
  assign _7 = and_25_out ? 16'h3f3 : 16'bz;  // Driver driver_87
  assign _5 = and_26_out ? 16'h4a3f : 16'bz;  // Driver driver_88
  assign _6 = and_26_out ? 16'hf0 : 16'bz;  // Driver driver_89
  assign _7 = and_26_out ? 16'h4803 : 16'bz;  // Driver driver_90
  assign _5 = and_27_out ? 16'h4a3f : 16'bz;  // Driver driver_91
  assign _6 = and_27_out ? 16'h2fb : 16'bz;  // Driver driver_92
  assign _7 = and_27_out ? 16'h3f3 : 16'bz;  // Driver driver_93
  assign _4 = and_28_out ? 16'h4a3f : 16'bz;  // Driver driver_94
  assign _5 = and_28_out ? 16'hf0 : 16'bz;  // Driver driver_95
  assign _6 = and_28_out ? 16'h4803 : 16'bz;  // Driver driver_96
  assign _7 = and_28_out ? 16'hfc : 16'bz;  // Driver driver_97
  assign _4 = and_29_out ? 16'h4a3f : 16'bz;  // Driver driver_98
  assign _5 = and_29_out ? 16'h2fb : 16'bz;  // Driver driver_99
  assign _6 = and_29_out ? 16'h3f3 : 16'bz;  // Driver driver_100
  assign _7 = and_29_out ? 16'hfc : 16'bz;  // Driver driver_101
  assign _6 = and_30_out ? 16'hf0 : 16'bz;  // Driver driver_102
  assign _7 = and_30_out ? 16'h4a3f : 16'bz;  // Driver driver_103
  assign _6 = and_31_out ? 16'hf0 : 16'bz;  // Driver driver_104
  assign _7 = and_31_out ? 16'h3cc : 16'bz;  // Driver driver_105
  assign _6 = and_32_out ? 16'hf0 : 16'bz;  // Driver driver_106
  assign _7 = and_32_out ? 16'ha0cc : 16'bz;  // Driver driver_107
  assign _5 = and_33_out ? 16'hf0 : 16'bz;  // Driver driver_108
  assign _6 = and_33_out ? 16'h4a3f : 16'bz;  // Driver driver_109
  assign _7 = and_33_out ? 16'hfc : 16'bz;  // Driver driver_110
  assign _5 = and_34_out ? 16'hf0 : 16'bz;  // Driver driver_111
  assign _6 = and_34_out ? 16'h3cc : 16'bz;  // Driver driver_112
  assign _7 = and_34_out ? 16'hfc : 16'bz;  // Driver driver_113
  assign _6 = and_35_out ? 16'h63b : 16'bz;  // Driver driver_114
  assign _7 = and_35_out ? 16'h4a3f : 16'bz;  // Driver driver_115
  assign _6 = and_36_out ? 16'h63b : 16'bz;  // Driver driver_116
  assign _7 = and_36_out ? 16'h3cc : 16'bz;  // Driver driver_117
  assign _6 = and_37_out ? 16'h63b : 16'bz;  // Driver driver_118
  assign _7 = and_37_out ? 16'ha0cc : 16'bz;  // Driver driver_119
  assign _0 = and_38_out ? 16'h300 : 16'bz;  // Driver driver_120
  assign _1 = and_38_out ? 16'h300 : 16'bz;  // Driver driver_121
  assign _2 = and_38_out ? 16'h300 : 16'bz;  // Driver driver_122
  assign _3 = and_38_out ? 16'h300 : 16'bz;  // Driver driver_123
  assign _4 = and_38_out ? 16'h300 : 16'bz;  // Driver driver_124
  assign _5 = and_38_out ? 16'h300 : 16'bz;  // Driver driver_125
  assign _6 = and_38_out ? 16'h300 : 16'bz;  // Driver driver_126
  assign _7 = and_38_out ? 16'h300 : 16'bz;  // Driver driver_127
  assign _0 = nor_1_out ? 16'hf3 : 16'bz;  // Driver driver_128
  assign _1 = nor_1_out ? 16'hff : 16'bz;  // Driver driver_129
  assign _2 = nor_1_out ? 16'h24cc : 16'bz;  // Driver driver_130
  assign _3 = nor_1_out ? 16'h63b : 16'bz;  // Driver driver_131
  assign _4 = nor_1_out ? 16'h4803 : 16'bz;  // Driver driver_132
  assign _5 = nor_1_out ? 16'h3cf : 16'bz;  // Driver driver_133
  assign _6 = nor_1_out ? 16'h24cc : 16'bz;  // Driver driver_134
  assign _7 = nor_1_out ? 16'h4803 : 16'bz;  // Driver driver_135
  PullDown #(.Bits(16)) pulldown_1 (.out(_1));
  PullDown #(.Bits(16)) pulldown_2 (.out(_0));
  PullDown #(.Bits(16)) pulldown_3 (.out(_2));
  PullDown #(.Bits(16)) pulldown_4 (.out(_3));
  PullDown #(.Bits(16)) pulldown_5 (.out(_4));
  PullDown #(.Bits(16)) pulldown_6 (.out(_5));
  PullDown #(.Bits(16)) pulldown_7 (.out(_6));
  PullDown #(.Bits(16)) pulldown_8 (.out(_7));

  assign D0 = 1'b0;
  assign D1 = 1'b0;
  assign D2 = 1'b0;
  assign D3 = 1'b0;
  assign D4 = 1'b0;
  assign D5 = 1'b0;
  assign D6 = 1'b0;
  assign D7 = 1'b0;

  // Notes on the sheet:
  //   INSTR: default 4099
  //   LUI
  //   JAL
  //   ADD
  //   SUB
  //   AND
  //   OR
  //   XOR
  //   ADDI
  //   ANDI
  //   ORI
  //   XORI
  //   SLL
  //   SRL
  //   SRA
  //   SLLI
  //   SRLI
  //   SRAI
  //   SLT
  //   SLTU
  //   SLTI
  //   SLTIU
  //   AUIPC
  //   JALR
  //   BEQ
  //   BNE
  //   BLT
  //   BGE
  //   BLTU
  //   BGEU
  //   LB
  //   LH
  //   LW
  //   LBU
  //   LHU
  //   SB
  //   SH
  //   SW
  //   A
  //   -
  //   B
  //   C
  //   D
  //   E
  //   F
  //   G
  //   H
  //   I
  //   J
  //   K
  //   L
  //   M
  //   N
  //   O
  //   P
  //   Q
  //   R
  //   S
  //   T
  //   U
  //   V
  //   W
  //   X
  //   Y
  //   Z
endmodule
