// Digital circuit RV32I-Memory-Control.dig as structural Verilog
module RV32I_Memory_Control (
  input  [31:0] INSTR,
  input  Normal,
  input  Run,
  output MEMORY_HOLD,
  output MEMORY_EN,
  output ALU_SET_REGISTER,
  output ALU_SET_MEM_R_W_A,
  output WRITE_TO_MEMORY
);

  wire rv32i_instruction_decoder_1_p3;
  wire [3:1] rv32i_instruction_decoder_1_p2;

  // RV32I_Instruction_Decoder rv32i_instruction_decoder_1: pin names not known; wires that end beside it: INSTR, {rv32i_instruction_decoder_1_p2, ALU_SET_REGISTER}, rv32i_instruction_decoder_1_p3
  and and_1 (MEMORY_HOLD, ~INSTR[4], INSTR[5], INSTR[6]);  // And
  and and_2 (MEMORY_EN, Normal, Run);
  and and_3 (ALU_SET_MEM_R_W_A, rv32i_instruction_decoder_1_p2[3], Normal);
  and and_4 (WRITE_TO_MEMORY, rv32i_instruction_decoder_1_p2[3], rv32i_instruction_decoder_1_p3, Normal);
endmodule
