// Digital circuit RV32I-Memory-Instruction-Decoder.dig as structural Verilog
module RV32I_Memory_Instruction_Decoder (
  input  [31:0] IN,
  output [2:0] DATA_SOURCE,
  output WRITE_MEMORY,
  output MEMORY_ACCESS
);

  and and_1 (DATA_SOURCE[0], ~IN[3], IN[4], ~IN[6]);  // And
  and and_2 (DATA_SOURCE[1], ~IN[2], ~IN[3], IN[4], ~IN[6], IN[13], ~IN[14]);  // And
  and and_3 (DATA_SOURCE[2], IN[0], IN[1], ~IN[2], ~IN[3], ~IN[4], ~IN[5], ~IN[6]);  // And
  and and_4 (WRITE_MEMORY, ~IN[2], ~IN[3], ~IN[4], IN[5], ~IN[6]);  // And
  and and_5 (MEMORY_ACCESS, ~IN[2], ~IN[3], ~IN[4], ~IN[6]);  // And

  // Notes on the sheet:
  //   IN: default 20191123
endmodule
