// Digital circuit RV32I-Register-Reserve.dig as structural Verilog
module RV32I_Register_Reserve (
  input  [31:0] INSTR,
  input  CLC,
  input  RE,
  input  RO,
  output HOLD
);

  wire and_1_out, and_2_out, comparator_1_eq, comparator_2_eq, comparator_3_eq, comparator_4_eq, or_1_out,
       or_2_out, or_3_out, or_4_out;
  wire [4:0] REGISTER_RESERVE_EVEN_q, REGISTER_RESERVE_ODD_q;

  Register #(.Bits(5)) REGISTER_RESERVE_EVEN (.D(INSTR[11:7]), .C(CLC), .en(RE), .Q(REGISTER_RESERVE_EVEN_q));
  Register #(.Bits(5)) REGISTER_RESERVE_ODD (.D(INSTR[11:7]), .C(CLC), .en(RO), .Q(REGISTER_RESERVE_ODD_q));
  or or_1 (or_1_out, INSTR[15], INSTR[16], INSTR[17], INSTR[18], INSTR[19]);
  or or_2 (or_2_out, INSTR[20], INSTR[21], INSTR[22], INSTR[23], INSTR[24]);
  Comparator #(.Bits(5)) comparator_1 (
    .a(REGISTER_RESERVE_EVEN_q), .b(INSTR[19:15]), .eq(comparator_1_eq));  // open: gt, lt
  Comparator #(.Bits(5)) comparator_2 (
    .a(REGISTER_RESERVE_ODD_q), .b(INSTR[19:15]), .eq(comparator_2_eq));  // open: gt, lt
  Comparator #(.Bits(5)) comparator_3 (
    .a(REGISTER_RESERVE_EVEN_q), .b(INSTR[24:20]), .eq(comparator_3_eq));  // open: gt, lt
  Comparator #(.Bits(5)) comparator_4 (
    .a(REGISTER_RESERVE_ODD_q), .b(INSTR[24:20]), .eq(comparator_4_eq));  // open: gt, lt
  or or_3 (or_3_out, comparator_2_eq, comparator_1_eq);
  or or_4 (or_4_out, comparator_4_eq, comparator_3_eq);
  and and_1 (and_1_out, or_3_out, or_1_out);
  and and_2 (and_2_out, or_4_out, or_2_out);
  or or_5 (HOLD, and_1_out, and_2_out);
endmodule
