// Digital circuit RV32I-System.dig as structural Verilog
module RV32I_System (
  input  CLC
);

  wire _6_digit_display_1_d0, _6_digit_display_1_d1, _6_digit_display_1_d2, _6_digit_display_1_d3,
       _6_digit_display_1_d4, _6_digit_display_1_d5, _6_digit_display_2_d0, _6_digit_display_2_d1,
       _6_digit_display_2_d2, _6_digit_display_2_d3, _6_digit_display_2_d4, _6_digit_display_2_d5,
       _6_digit_display_3_d0, _6_digit_display_3_d1, _6_digit_display_3_d2, _6_digit_display_3_d3,
       _6_digit_display_3_d4, _6_digit_display_3_d5, _8_digit_display_1_d0, _8_digit_display_1_d1,
       _8_digit_display_1_d2, _8_digit_display_1_d3, _8_digit_display_1_d4, _8_digit_display_1_d5,
       _8_digit_display_1_d6, _8_digit_display_1_d7, _8_digit_display_2_d0, _8_digit_display_2_d1,
       _8_digit_display_2_d2, _8_digit_display_2_d3, _8_digit_display_2_d4, _8_digit_display_2_d5,
       _8_digit_display_2_d6, _8_digit_display_2_d7, _8_digit_display_3_d0, _8_digit_display_3_d1,
       _8_digit_display_3_d2, _8_digit_display_3_d3, _8_digit_display_3_d4, _8_digit_display_3_d5,
       _8_digit_display_3_d6, _8_digit_display_3_d7, _8_digit_display_4_d0, _8_digit_display_4_d1,
       _8_digit_display_4_d2, _8_digit_display_4_d3, _8_digit_display_4_d4, _8_digit_display_4_d5,
       _8_digit_display_4_d6, _8_digit_display_4_d7, _8_digit_display_5_d0, _8_digit_display_5_d1,
       _8_digit_display_5_d2, _8_digit_display_5_d3, _8_digit_display_5_d4, _8_digit_display_5_d5,
       _8_digit_display_5_d6, _8_digit_display_5_d7, _8_digit_display_6_d0, _8_digit_display_6_d1,
       _8_digit_display_6_d2, _8_digit_display_6_d3, _8_digit_display_6_d4, _8_digit_display_6_d5,
       _8_digit_display_6_d6, _8_digit_display_6_d7, ALU_A, ALU_B, ALU_INSTR, ALU_Y,
       binary_bcd_converter_1_d0, binary_bcd_converter_1_d1, binary_bcd_converter_2_d0,
       binary_bcd_converter_2_d1, BOOT_CNT_EN, BOOT_CNT_SET_MEM_ADDR, BOOT_COMPLETE, BOOT_COUNTER_OVERFLOW,
       COMP, CPU_p19, CPU_p21, GO, NORMAL, not_1_out, or_1_out, P_out, R_out, ROM_WRITE_MEM, RUN, S_out,
       T_out, undriven;
  wire [3:0] _6_digit_display_1__0, _6_digit_display_1__1, _6_digit_display_1__2, _6_digit_display_1__3,
       _6_digit_display_1__4, _6_digit_display_1__5, _6_digit_display_2__0, _6_digit_display_2__1,
       _6_digit_display_2__2, _6_digit_display_2__3, _6_digit_display_2__4, _6_digit_display_2__5,
       _6_digit_display_3__0, _6_digit_display_3__1, _6_digit_display_3__2, _6_digit_display_3__3,
       _6_digit_display_3__4, _6_digit_display_3__5, _8_digit_display_1__0, _8_digit_display_1__1,
       _8_digit_display_1__2, _8_digit_display_1__3, _8_digit_display_1__4, _8_digit_display_1__5,
       _8_digit_display_1__6, _8_digit_display_1__7, _8_digit_display_2__0, _8_digit_display_2__1,
       _8_digit_display_2__2, _8_digit_display_2__3, _8_digit_display_2__4, _8_digit_display_2__5,
       _8_digit_display_2__6, _8_digit_display_2__7, _8_digit_display_3__0, _8_digit_display_3__1,
       _8_digit_display_3__2, _8_digit_display_3__3, _8_digit_display_3__4, _8_digit_display_3__5,
       _8_digit_display_3__6, _8_digit_display_3__7, _8_digit_display_4__0, _8_digit_display_4__1,
       _8_digit_display_4__2, _8_digit_display_4__3, _8_digit_display_4__4, _8_digit_display_4__5,
       _8_digit_display_4__6, _8_digit_display_4__7, _8_digit_display_5__0, _8_digit_display_5__1,
       _8_digit_display_5__2, _8_digit_display_5__3, _8_digit_display_5__4, _8_digit_display_5__5,
       _8_digit_display_5__6, _8_digit_display_5__7, _8_digit_display_6__0, _8_digit_display_6__1,
       _8_digit_display_6__2, _8_digit_display_6__3, _8_digit_display_6__4, _8_digit_display_6__5,
       _8_digit_display_6__6, _8_digit_display_6__7, binary_bcd_converter_1__0, binary_bcd_converter_1__1,
       binary_bcd_converter_2__0, binary_bcd_converter_2__1;
  wire [4:0] HELD_REGISTER_0, HELD_REGISTER_1;
  wire [23:0] BOOT_CNT, CPU_p20, MEM_R_W_A, PC_OUT;
  wire [31:0] CPU_p22, INSTR_DECODE, INSTR_EXECUTE, INSTR_MEMORY, INSTR_WRITE, MEM_R_W, ROM;

  Counter #(.Bits(24)) u_BOOT_CNT (
    .en(BOOT_CNT_EN), .C(CLC), .clr(NORMAL), .out(BOOT_CNT), .ovf(BOOT_COUNTER_OVERFLOW));
  Seven_Seg_Hex seven_seg_hex_1 (.d(_8_digit_display_1__0), .dp(_8_digit_display_1_d0));
  Seven_Seg_Hex seven_seg_hex_2 (.d(_8_digit_display_1__1), .dp(_8_digit_display_1_d1));
  _8_Digit_Display _8_digit_display_1 (
    .I(ROM), ._0(_8_digit_display_1__0), .D0(_8_digit_display_1_d0), ._1(_8_digit_display_1__1),
    .D1(_8_digit_display_1_d1), ._2(_8_digit_display_1__2), .D2(_8_digit_display_1_d2),
    ._3(_8_digit_display_1__3), .D3(_8_digit_display_1_d3), ._4(_8_digit_display_1__4),
    .D4(_8_digit_display_1_d4), ._5(_8_digit_display_1__5), .D5(_8_digit_display_1_d5),
    ._6(_8_digit_display_1__6), .D6(_8_digit_display_1_d6), ._7(_8_digit_display_1__7),
    .D7(_8_digit_display_1_d7));
  Button S (.out(S_out));
  Button R (.out(R_out));
  Button T (.out(T_out));
  Seven_Seg_Hex seven_seg_hex_3 (.d(_6_digit_display_1__0), .dp(_6_digit_display_1_d0));
  Seven_Seg_Hex seven_seg_hex_4 (.d(_6_digit_display_1__1), .dp(_6_digit_display_1_d1));
  Seven_Seg_Hex seven_seg_hex_5 (.d(_8_digit_display_1__2), .dp(_8_digit_display_1_d2));
  Seven_Seg_Hex seven_seg_hex_6 (.d(_8_digit_display_1__3), .dp(_8_digit_display_1_d3));
  _6_Digit_Display _6_digit_display_1 (
    .I(BOOT_CNT), ._0(_6_digit_display_1__0), .D0(_6_digit_display_1_d0), ._1(_6_digit_display_1__1),
    .D1(_6_digit_display_1_d1), ._2(_6_digit_display_1__2), .D2(_6_digit_display_1_d2),
    ._3(_6_digit_display_1__3), .D3(_6_digit_display_1_d3), ._4(_6_digit_display_1__4),
    .D4(_6_digit_display_1_d4), ._5(_6_digit_display_1__5), .D5(_6_digit_display_1_d5));
  LED led_1 (.in(NORMAL));
  LED led_2 (.in(RUN));
  LED led_3 (.in(GO));
  Button P (.out(P_out));
  Seven_Seg_Hex seven_seg_hex_7 (.d(_6_digit_display_1__2), .dp(_6_digit_display_1_d2));
  Seven_Seg_Hex seven_seg_hex_8 (.d(_6_digit_display_1__3), .dp(_6_digit_display_1_d3));
  Seven_Seg_Hex seven_seg_hex_9 (.d(_8_digit_display_1__4), .dp(_8_digit_display_1_d4));
  Seven_Seg_Hex seven_seg_hex_10 (.d(_8_digit_display_1__5), .dp(_8_digit_display_1_d5));
  RV32I_Control rv32i_control_1 (
    .START(S_out), .PAUSE(P_out), .RESET(R_out), .HOLD(BOOT_COMPLETE), .SET_ERROR(BOOT_COUNTER_OVERFLOW),
    .BC(CLC), .BCO(T_out), .NORMAL(NORMAL), .RUN(RUN), .GO(BOOT_CNT_EN), .ERROR(BOOT_CNT_SET_MEM_ADDR),
    .BCE(ROM_WRITE_MEM));  // open: CLC, RUN_OVERRIDE, BC_SET_R_W_A, ROM_SET_MEM_R_W
  Seven_Seg_Hex seven_seg_hex_11 (.d(_6_digit_display_1__4), .dp(_6_digit_display_1_d4));
  Seven_Seg_Hex seven_seg_hex_12 (.d(_6_digit_display_1__5), .dp(_6_digit_display_1_d5));
  Seven_Seg_Hex seven_seg_hex_13 (.d(_8_digit_display_1__6), .dp(_8_digit_display_1_d6));
  Seven_Seg_Hex seven_seg_hex_14 (.d(_8_digit_display_1__7), .dp(_8_digit_display_1_d7));
  ROM #(.AddrBits(24), .isProgramMemory("true"), .Bits(32)) u_ROM (.A(BOOT_CNT), .sel(1'b1), .D(ROM));
  Comparator #(.Bits(24)) comparator_1 (.a(BOOT_CNT), .b(24'h60), .eq(BOOT_COMPLETE));  // open: gt, lt
  Seven_Seg_Hex seven_seg_hex_15 (.d(_8_digit_display_2__0), .dp(_8_digit_display_2_d0));
  Seven_Seg_Hex seven_seg_hex_16 (.d(_6_digit_display_2__0), .dp(_6_digit_display_2_d0));
  Seven_Seg_Hex seven_seg_hex_17 (.d(_8_digit_display_2__1), .dp(_8_digit_display_2_d1));
  Seven_Seg_Hex seven_seg_hex_18 (.d(_8_digit_display_2__2), .dp(_8_digit_display_2_d2));
  _8_Digit_Display _8_digit_display_2 (
    .I(MEM_R_W), ._0(_8_digit_display_2__0), .D0(_8_digit_display_2_d0), ._1(_8_digit_display_2__1),
    .D1(_8_digit_display_2_d1), ._2(_8_digit_display_2__2), .D2(_8_digit_display_2_d2),
    ._3(_8_digit_display_2__3), .D3(_8_digit_display_2_d3), ._4(_8_digit_display_2__4),
    .D4(_8_digit_display_2_d4), ._5(_8_digit_display_2__5), .D5(_8_digit_display_2_d5),
    ._6(_8_digit_display_2__6), .D6(_8_digit_display_2_d6), ._7(_8_digit_display_2__7),
    .D7(_8_digit_display_2_d7));
  Seven_Seg_Hex seven_seg_hex_19 (.d(_6_digit_display_2__1), .dp(_6_digit_display_2_d1));
  Seven_Seg_Hex seven_seg_hex_20 (.d(_6_digit_display_2__2), .dp(_6_digit_display_2_d2));
  Seven_Seg_Hex seven_seg_hex_21 (.d(_8_digit_display_2__3), .dp(_8_digit_display_2_d3));
  Seven_Seg_Hex seven_seg_hex_22 (.d(_8_digit_display_2__4), .dp(_8_digit_display_2_d4));
  _6_Digit_Display _6_digit_display_2 (
    .I(MEM_R_W_A), ._0(_6_digit_display_2__0), .D0(_6_digit_display_2_d0), ._1(_6_digit_display_2__1),
    .D1(_6_digit_display_2_d1), ._2(_6_digit_display_2__2), .D2(_6_digit_display_2_d2),
    ._3(_6_digit_display_2__3), .D3(_6_digit_display_2_d3), ._4(_6_digit_display_2__4),
    .D4(_6_digit_display_2_d4), ._5(_6_digit_display_2__5), .D5(_6_digit_display_2_d5));
  Seven_Seg_Hex seven_seg_hex_23 (.d(_6_digit_display_2__3), .dp(_6_digit_display_2_d3));
  Seven_Seg_Hex seven_seg_hex_24 (.d(_6_digit_display_2__4), .dp(_6_digit_display_2_d4));
  Seven_Seg_Hex seven_seg_hex_25 (.d(_8_digit_display_2__5), .dp(_8_digit_display_2_d5));
  Seven_Seg_Hex seven_seg_hex_26 (.d(_8_digit_display_2__6), .dp(_8_digit_display_2_d6));
  Seven_Seg_Hex seven_seg_hex_27 (.d(_6_digit_display_2__5), .dp(_6_digit_display_2_d5));
  Seven_Seg_Hex seven_seg_hex_28 (.d(_8_digit_display_2__7), .dp(_8_digit_display_2_d7));
  Seven_Seg_Hex seven_seg_hex_29 (.d(_8_digit_display_3__0), .dp(_8_digit_display_3_d0));
  Seven_Seg_Hex seven_seg_hex_30 (.d(_8_digit_display_3__1), .dp(_8_digit_display_3_d1));
  _8_Digit_Display _8_digit_display_3 (
    .I(INSTR_DECODE), ._0(_8_digit_display_3__0), .D0(_8_digit_display_3_d0), ._1(_8_digit_display_3__1),
    .D1(_8_digit_display_3_d1), ._2(_8_digit_display_3__2), .D2(_8_digit_display_3_d2),
    ._3(_8_digit_display_3__3), .D3(_8_digit_display_3_d3), ._4(_8_digit_display_3__4),
    .D4(_8_digit_display_3_d4), ._5(_8_digit_display_3__5), .D5(_8_digit_display_3_d5),
    ._6(_8_digit_display_3__6), .D6(_8_digit_display_3_d6), ._7(_8_digit_display_3__7),
    .D7(_8_digit_display_3_d7));
  Seven_Seg_Hex seven_seg_hex_31 (.d(_6_digit_display_3__0), .dp(_6_digit_display_3_d0));
  Seven_Seg_Hex seven_seg_hex_32 (.d(_6_digit_display_3__1), .dp(_6_digit_display_3_d1));
  Seven_Seg_Hex seven_seg_hex_33 (.d(_8_digit_display_3__2), .dp(_8_digit_display_3_d2));
  Seven_Seg_Hex seven_seg_hex_34 (.d(_8_digit_display_3__3), .dp(_8_digit_display_3_d3));
  _6_Digit_Display _6_digit_display_3 (
    .I(PC_OUT), ._0(_6_digit_display_3__0), .D0(_6_digit_display_3_d0), ._1(_6_digit_display_3__1),
    .D1(_6_digit_display_3_d1), ._2(_6_digit_display_3__2), .D2(_6_digit_display_3_d2),
    ._3(_6_digit_display_3__3), .D3(_6_digit_display_3_d3), ._4(_6_digit_display_3__4),
    .D4(_6_digit_display_3_d4), ._5(_6_digit_display_3__5), .D5(_6_digit_display_3_d5));
  Seven_Seg_Hex seven_seg_hex_35 (.d(_6_digit_display_3__2), .dp(_6_digit_display_3_d2));
  Seven_Seg_Hex seven_seg_hex_36 (.d(_6_digit_display_3__3), .dp(_6_digit_display_3_d3));
  Seven_Seg_Hex seven_seg_hex_37 (.d(_8_digit_display_3__4), .dp(_8_digit_display_3_d4));
  Seven_Seg_Hex seven_seg_hex_38 (.d(_8_digit_display_3__5), .dp(_8_digit_display_3_d5));
  Seven_Seg_Hex seven_seg_hex_39 (.d(_6_digit_display_3__4), .dp(_6_digit_display_3_d4));
  Seven_Seg_Hex seven_seg_hex_40 (.d(_6_digit_display_3__5), .dp(_6_digit_display_3_d5));
  Seven_Seg_Hex seven_seg_hex_41 (.d(_8_digit_display_3__6), .dp(_8_digit_display_3_d6));
  Seven_Seg_Hex seven_seg_hex_42 (.d(_8_digit_display_3__7), .dp(_8_digit_display_3_d7));
  or or_1 (or_1_out, ~NORMAL, CPU_p21);  // Or
  Seven_Seg_Hex seven_seg_hex_43 (.d(_8_digit_display_4__0), .dp(_8_digit_display_4_d0));
  Seven_Seg_Hex seven_seg_hex_44 (.d(_8_digit_display_4__1), .dp(_8_digit_display_4_d1));
  Seven_Seg_Hex seven_seg_hex_45 (.d(_8_digit_display_4__2), .dp(_8_digit_display_4_d2));
  _8_Digit_Display _8_digit_display_4 (
    .I(INSTR_EXECUTE), ._0(_8_digit_display_4__0), .D0(_8_digit_display_4_d0), ._1(_8_digit_display_4__1),
    .D1(_8_digit_display_4_d1), ._2(_8_digit_display_4__2), .D2(_8_digit_display_4_d2),
    ._3(_8_digit_display_4__3), .D3(_8_digit_display_4_d3), ._4(_8_digit_display_4__4),
    .D4(_8_digit_display_4_d4), ._5(_8_digit_display_4__5), .D5(_8_digit_display_4_d5),
    ._6(_8_digit_display_4__6), .D6(_8_digit_display_4_d6), ._7(_8_digit_display_4__7),
    .D7(_8_digit_display_4_d7));
  assign MEM_R_W_A = BOOT_CNT_SET_MEM_ADDR ? BOOT_CNT : 24'bz;  // Driver driver_1
  assign MEM_R_W_A = CPU_p19 ? CPU_p20 : 24'bz;  // Driver driver_2
  Seven_Seg_Hex seven_seg_hex_46 (.d(_8_digit_display_4__3), .dp(_8_digit_display_4_d3));
  Seven_Seg_Hex seven_seg_hex_47 (.d(_8_digit_display_4__4), .dp(_8_digit_display_4_d4));
  not not_1 (not_1_out, or_1_out);
  PullDown #(.Bits(24)) pulldown_1 (.out(MEM_R_W_A));
  Seven_Seg_Hex seven_seg_hex_48 (.d(_8_digit_display_4__5), .dp(_8_digit_display_4_d5));
  Seven_Seg_Hex seven_seg_hex_49 (.d(_8_digit_display_4__6), .dp(_8_digit_display_4_d6));
  RAMDualAccess #(.AddrBits(24), .Bits(32)) Memory (
    .str(or_1_out), .C(CLC), .ld(not_1_out), .A1(MEM_R_W_A), .Din1(MEM_R_W), .A2(PC_OUT), .D1(MEM_R_W),
    .D2(INSTR_DECODE));
  Seven_Seg_Hex seven_seg_hex_50 (.d(_8_digit_display_4__7), .dp(_8_digit_display_4_d7));
  assign MEM_R_W = CPU_p21 ? CPU_p22 : 32'bz;  // Driver driver_3
  assign MEM_R_W = ROM_WRITE_MEM ? ROM : 32'bz;  // Driver driver_4
  SixteenSeg sixteenseg_1 ();  // open: led, dp
  Seven_Seg_Hex seven_seg_hex_51 (.d(_8_digit_display_5__0), .dp(_8_digit_display_5_d0));
  Seven_Seg_Hex seven_seg_hex_52 (.d(_8_digit_display_5__1), .dp(_8_digit_display_5_d1));
  _8_Digit_Display _8_digit_display_5 (
    .I(INSTR_MEMORY), ._0(_8_digit_display_5__0), .D0(_8_digit_display_5_d0), ._1(_8_digit_display_5__1),
    .D1(_8_digit_display_5_d1), ._2(_8_digit_display_5__2), .D2(_8_digit_display_5_d2),
    ._3(_8_digit_display_5__3), .D3(_8_digit_display_5_d3), ._4(_8_digit_display_5__4),
    .D4(_8_digit_display_5_d4), ._5(_8_digit_display_5__5), .D5(_8_digit_display_5_d5),
    ._6(_8_digit_display_5__6), .D6(_8_digit_display_5_d6), ._7(_8_digit_display_5__7),
    .D7(_8_digit_display_5_d7));
  Seven_Seg_Hex seven_seg_hex_53 (.d(_8_digit_display_5__2), .dp(_8_digit_display_5_d2));
  Seven_Seg_Hex seven_seg_hex_54 (.d(_8_digit_display_5__3), .dp(_8_digit_display_5_d3));
  // RV32I CPU: pin names not known; wires that end beside it: CLC, INSTR_DECODE, NORMAL, RUN, 1'b0, MEM_R_W, INSTR_EXECUTE, INSTR_MEMORY, INSTR_WRITE, GO, HELD_REGISTER_0, HELD_REGISTER_1, ALU_INSTR, ALU_A, ALU_B, ALU_Y, COMP, PC_OUT, CPU_p19, CPU_p20, CPU_p21, CPU_p22
  Seven_Seg_Hex seven_seg_hex_55 (.d(_8_digit_display_5__4), .dp(_8_digit_display_5_d4));
  Seven_Seg_Hex seven_seg_hex_56 (.d(_8_digit_display_5__5), .dp(_8_digit_display_5_d5));
  Seven_Seg_Hex seven_seg_hex_57 (.d(_8_digit_display_5__6), .dp(_8_digit_display_5_d6));
  Seven_Seg_Hex seven_seg_hex_58 (.d(_8_digit_display_5__7), .dp(_8_digit_display_5_d7));
  Seven_Seg_Hex seven_seg_hex_59 (.d(_8_digit_display_6__0), .dp(_8_digit_display_6_d0));
  Seven_Seg_Hex seven_seg_hex_60 (.d(_8_digit_display_6__1), .dp(_8_digit_display_6_d1));
  Seven_Seg_Hex seven_seg_hex_61 (.d(_8_digit_display_6__2), .dp(_8_digit_display_6_d2));
  _8_Digit_Display _8_digit_display_6 (
    .I(INSTR_WRITE), ._0(_8_digit_display_6__0), .D0(_8_digit_display_6_d0), ._1(_8_digit_display_6__1),
    .D1(_8_digit_display_6_d1), ._2(_8_digit_display_6__2), .D2(_8_digit_display_6_d2),
    ._3(_8_digit_display_6__3), .D3(_8_digit_display_6_d3), ._4(_8_digit_display_6__4),
    .D4(_8_digit_display_6_d4), ._5(_8_digit_display_6__5), .D5(_8_digit_display_6_d5),
    ._6(_8_digit_display_6__6), .D6(_8_digit_display_6_d6), ._7(_8_digit_display_6__7),
    .D7(_8_digit_display_6_d7));
  Seven_Seg_Hex seven_seg_hex_62 (.d(binary_bcd_converter_1__0), .dp(binary_bcd_converter_1_d0));
  Seven_Seg_Hex seven_seg_hex_63 (.d(binary_bcd_converter_1__1), .dp(binary_bcd_converter_1_d1));
  Seven_Seg_Hex seven_seg_hex_64 (.d(_8_digit_display_6__3), .dp(_8_digit_display_6_d3));
  Seven_Seg_Hex seven_seg_hex_65 (.d(_8_digit_display_6__4), .dp(_8_digit_display_6_d4));
  Binary_BCD_Converter binary_bcd_converter_1 (
    .I(HELD_REGISTER_1), ._0(binary_bcd_converter_1__0), .D0(binary_bcd_converter_1_d0),
    ._1(binary_bcd_converter_1__1), .D1(binary_bcd_converter_1_d1));
  Seven_Seg_Hex seven_seg_hex_66 (.d(binary_bcd_converter_2__0), .dp(binary_bcd_converter_2_d0));
  Seven_Seg_Hex seven_seg_hex_67 (.d(_8_digit_display_6__5), .dp(_8_digit_display_6_d5));
  Seven_Seg_Hex seven_seg_hex_68 (.d(_8_digit_display_6__6), .dp(_8_digit_display_6_d6));
  Seven_Seg_Hex seven_seg_hex_69 (.d(binary_bcd_converter_2__1), .dp(binary_bcd_converter_2_d1));
  Seven_Seg_Hex seven_seg_hex_70 (.d(_8_digit_display_6__7), .dp(_8_digit_display_6_d7));
  Binary_BCD_Converter binary_bcd_converter_2 (
    .I(HELD_REGISTER_0), ._0(binary_bcd_converter_2__0), .D0(binary_bcd_converter_2_d0),
    ._1(binary_bcd_converter_2__1), .D1(binary_bcd_converter_2_d1));
  Break break_1 (.brk(undriven));

  // Other names for the same wires on the sheet: ROM_A[23:0] = BOOT_CNT

  // Notes on the sheet:
  //   CLC: Hz: 10
  //   NORMAL
  //   RUN
  //   GO
  //   ROM
  //   PROGRAM LENGTH
  //   contents of ROM (hex, n*v repeats v):
  //   140006f,aaaaaaaa,0,0,0,0,0,0,0,0,0,0,0,0,0,0,0,0,0,0,1437,497,40848533,409405b3,b57633,
  //   b566b3,b54733,1341793,c55813,40b7d893,fff7c913,ffb97993,57ea13,ca1ab3,ca5b33,40ca5bb3,
  //   17b2c33,16bacb3,17b3d33,16bbdb3,bae13,b2e93,bbf13,263f93,100103,0,10123,111a3,104103,
  //   10223,112a3,101103,11323,123a3,105103,11423,124a3,0,13,fffff06f
  //   MEM R/W
  //   INSTR
  //   EXECUTE
  //   MEMORY
  //   WRITE
endmodule
