// Digital circuit RV32I-Write-Control.dig as structural Verilog
module RV32I_Write_Control (
  input  [31:0] INSTR,
  input  Normal,
  input  Run,
  output EXECUTE_HOLD,
  output REG_WRITE
);

  wire rv32i_write_instruction_decoder_1_reg_hold;

  RV32I_Write_Instruction_Decoder rv32i_write_instruction_decoder_1 (
    .IN(INSTR), .REG_HOLD(rv32i_write_instruction_decoder_1_reg_hold));
  and and_1 (EXECUTE_HOLD, ~INSTR[4], INSTR[5], INSTR[6]);  // And
  and and_2 (REG_WRITE, rv32i_write_instruction_decoder_1_reg_hold, Normal, Run);
endmodule
